# Fritzing sketch Coronavirus Wearable (saved by Fritzing 0.9.4)
breadboards: 1

parts:
  BAT1 = Battery Holders [package=battery-aa-kit]
  SG1 = Buzzer 12mm [package=buzzer-ccv-kit]
  S1 = Tilt Switch [package=THT]
  LED1 = smd LED [color="Red (633nm)" package="0805 [SMD]"]
  U1 = attiny85 [package=dip]
  S2 = SWITCH-MOMENTARY-2 [package=tactile-pth]
  R1 = Resistor [tolerance=±5% resistance=220 package="0805 [SMD]"]
  U2 = Vibration Motor- ROB-08449 [package=vibe-motor-10mm]
  Q1 = TRANSISTOR_NPN [package=to-92-ammo]

nets:
  N1: BAT1.+, U1.Pin_8
  N2: BAT1.-, SG1.2, S1.Pin_1, LED1.cathode, U1.Pin_4, S2.2, U2.-, Q1.C
  N3: SG1.1, U1.Pin_6
  N4: S1.Pin_2, U1.Pin_2
  N5: LED1.anode, R1.Pin_0
  N6: U1.Pin_3, R1.Pin_1
  N7: U1.Pin_5, Q1.B
  N8: U1.Pin_7, S2.1
  N9: U2.+, Q1.E
